# Fritzing sketch Lidar_Buck_USBToTTL_Wiring (saved by Fritzing 0.9.3b)

parts:
  U1 = LM2596 step down module
  USBTTL1 = USB TTL Serial Cable
  M1 = RPlidar A1M8 [package=THT]

nets:
  N1: U1.OUT+, M1.pin3
  N2: U1.OUT-, USBTTL1.GND, M1.pin4
  N3: USBTTL1.RX, M1.pin1
  N4: USBTTL1.TX, M1.pin2

custom parts:
  LM2596 step down module: LM2596 DC-DC step down power supply module 3 A.
  RPlidar A1M8: .The RPLIDAR A1 is the next generation low cost 360 degree 2D laser scanner (LIDAR) solution developed by SLAMTEC. It can take up to 4000 samples of laser ranging per second with high rotation speed. And equipped with SLAMTEC patented OPTMAG technology, it breakouts the life limitation of traditional LIDAR system so as to work stably for a long time.
