# Fritzing sketch Wiring (saved by Fritzing 0.9.3b)
# 18650 Li-ion Battery: CC-BY Dr Kristofer Chan, King's College London/Remote-research.org
breadboards: 1

parts:
  Part1 = Arduino Mega ADK (Rev3)
  J1 = Basic Servo
  J2 = Basic Servo
  J3 = Basic Servo
  J4 = Basic Servo
  J5 = Basic Servo
  Part2 = 16-Channel 12-bit PWM Servo Driver - I2C [part_number=815]
  A1 = DM860A Stepper Motor Driver
  M1 = Stepper Motor - Bipolar
  HLK-PM1 = HLK-PM12 [part_number=HLK-PM12]
  HC-SR04_Sensor_1 = HC-SR04 Ultrasonic Distance Sensor
  M2 = RioRand LM2596
  M3 = RioRand LM2596
  M4 = RioRand LM2596
  J6 = Basic Servo
  Raspberry_Pi_1 = Raspberry Pi 4 [part_number=RPI-4-b]
  M5 = RioRand LM2596
  L298N1 = L298N DC motor driver
  L298N2 = L298N DC motor driver
  M6 = DC Motor
  M7 = DC Motor
  M8 = RioRand LM2596
  J7 = Piezo Speaker
  Mod1 = 3S-BMS
  BAT1 = 18650 Li-ion Battery [package=battery-18650]
  BAT2 = 18650 Li-ion Battery [package=battery-18650]
  BAT3 = 18650 Li-ion Battery [package=battery-18650]
  BAT4 = 18650 Li-ion Battery [package=battery-18650]
  BAT5 = 18650 Li-ion Battery [package=battery-18650]
  BAT6 = 18650 Li-ion Battery [package=battery-18650]
  BAT7 = 18650 Li-ion Battery [package=battery-18650]
  BAT8 = 18650 Li-ion Battery [package=battery-18650]
  BAT9 = 18650 Li-ion Battery [package=battery-18650]
  BAT10 = 18650 Li-ion Battery [package=battery-18650]
  BAT11 = 18650 Li-ion Battery [package=battery-18650]
  BAT12 = 18650 Li-ion Battery [package=battery-18650]

nets:
  N1: Part1.D21/SCL, Part2.SCL
  N2: Part1.D20/SDA, Part2.SDA
  N3: Part1.D11_PWM, L298N2.IN2
  N4: Part1.D10_PWM, L298N2.IN1
  N5: Part1.D8_PWM, L298N1.IN2
  N6: Part1.GND, M3.Pin_4
  N7: Part1.VIN, M3.Pin_3
  N8: Part1.D2_PWM, Part2.OE
  N9: Part1.D3_PWM, A1.PUL+(+5V)
  N10: Part1.D4_PWM, A1.DIR+(+5V)
  N11: Part1.D5_PWM, A1.ENBL+(+5V)
  N12: Part1.D6_PWM, J7.pin2
  N13: Part1.D7_PWM, L298N1.IN1
  N14: Part1.D23, HC-SR04_Sensor_1.ECHO
  N15: Part1.D25, HC-SR04_Sensor_1.TRIG
  GND: J1.gnd, J2.gnd, J3.gnd, J4.gnd, J5.gnd, Part2.GND, M4.Pin_4, J6.gnd, J7.pin1
  VCC: J1.vcc, J2.vcc, J3.vcc, J4.vcc, J5.vcc, Part2.5.0V, Part2.VCC, M4.Pin_3, J6.vcc
  N16: J1.pulse, Part2.PWM15
  N17: J2.pulse, Part2.PWM13
  N18: J3.pulse, Part2.PWM14
  N19: J4.pulse, Part2.PWM11
  N20: J5.pulse, Part2.PWM12
  N21: Part2.PWM10, J6.pulse
  N22: A1.B-, M1.D
  N23: A1.B+, M1.B
  N24: A1.A-, M1.C
  N25: A1.A+, M1.A
  12V: A1.VDC, HLK-PM1.+Vo, M2.Pin_1, M3.Pin_1, M4.Pin_1, M5.Pin_1, L298N1.12V, L298N2.12V, M8.Pin_1, Mod1.+
  N26: A1.ENBL-(ENB), A1.DIR-(DIR), A1.PUL-(PUL)
  GND_2: HLK-PM1.-Vo, M2.Pin_2, M3.Pin_2, M4.Pin_2, M5.Pin_2, L298N1.GND, L298N2.GND, M8.Pin_2, M8.Pin_4, Mod1.-
  N27: HC-SR04_Sensor_1.VCC, M2.Pin_3
  N28: HC-SR04_Sensor_1.GND, M2.Pin_4
  N29: Raspberry_Pi_1.GPIO3, Raspberry_Pi_1.GND, M5.Pin_4
  N30: Raspberry_Pi_1.5V, M5.Pin_3
  N31: L298N1.OUT1, M6.pin_2
  N32: L298N1.OUT2, M6.pin_1
  N33: L298N1.5V, M8.Pin_3
  N34: L298N2.OUT1, M7.pin_2
  N35: L298N2.OUT2, M7.pin_1
  N36: Mod1.0V, BAT1.-, BAT2.-, BAT3.-, BAT4.-
  N37: Mod1.4.2V, BAT1.+, BAT2.+, BAT3.+, BAT4.+, BAT5.-, BAT6.-, BAT7.-, BAT8.-
  N38: Mod1.8.4V, BAT5.+, BAT6.+, BAT7.+, BAT8.+, BAT9.-, BAT10.-, BAT11.-, BAT12.-
  N39: Mod1.12.6V, BAT9.+, BAT11.+, BAT12.+

custom parts:
  16-Channel 12-bit PWM Servo Driver - I2C: You want to make a cool robot, maybe a hexapod walker, or maybe just a piece of art with a lot of moving parts. Or maybe you want to drive a lot of LEDs with precise PWM output. Using only two pins, control 16 free-running PWM outputs! You can even chain up 62 breakouts to control up to 992 PWM outputs.
  DM860A Stepper Motor Driver: DM860A is a type of two-phase hybrid stepping motor driver, The drive voltage of which is from 24VDC to 80VDC. It is designed for use with 2-phase hybrid stepper motor of all kinds with 57mm to 110mm outside diameter and less than 8.0A phase current. Mar 2023: Correct pcb layerId as the part won't save correctly in a .fzz file as is.
  Raspberry Pi 4: The RPi4, a faster version of the awesome Raspberry Pi 2 B ARM Board with 40 pin gpio. Ready for special Raspberry Pi B+ and RPi2 Hat (Hardware attached (on) top)
  L298N DC motor driver: 2x DC motor driver with 78M05 positive voltage regulator (7..35 V) L298N: max 46 V, 2 A Set 5 V Enable jumper to enable 5 V regultor (needed for the L298N) and +5 V output at screw terminal or supply external +5 V at screw terminal Set ENA and/or ENB to +5 V to enable motor permanently or supply ENA and/or ENB with PWM signal IN1 and IN2 set rotation directory for motor A (OUT1/OUT2) IN2 and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
  3S-BMS: 3S-BMS LIPO battery charger / protection unit. Note pcb does not match the board as it will likely connect with wires, so pcb is 6 pads suitable for .1in header pins.
  18650 Li-ion Battery: 18650 li-ion Battery Standard 18650 battery with interactive connectors Creative Common Attribution 4.0 International (CC-BY 4.0) license. Any use of this part requires attribution of Dr Kristofer Chan, Department of Geography, King's College London. Contact kristofer.chan [at] kcl.ac.uk OR kris [at] remote-research.org for further information.
